# Fritzing sketch INA169_Arduino_Example (saved by Fritzing 0.8.3b)
breadboards: 1

parts:
  Part1 = Arduino Uno (Rev3)
  R1 = Resistor [tolerance=±5% resistance=330 package=THT]
  LED1 = LED - 5mm [color="Red (633nm)" package="5 mm [THT]"]
  Part2 = INA169 Current Sensor Breakout [part_number=BOB-12040]

nets:
  N1: Part1.A0, Part2.VOUT
  5V: Part1.5V, Part2.VIN+, Part2.VCC
  GND: Part1.GND, LED1.cathode, Part2.GND
  N2: R1.Pin_0, Part2.VIN-
  N3: R1.Pin_1, LED1.anode

custom parts:
  INA169 Current Sensor Breakout: INA169 Current Sensor Breakout Board
